// Logisim project Caculation.circ as structural Verilog: 1 circuit, main circuit main
module main (
  input  in_1,
  input  [12:0] year_in,
  input  in_3,
  input  rst,
  input  Go_Current,
  input  [2:0] State,
  output [12:0] Output,
  output [2:0] out_8,
  output ERR,
  output Go_Next
);

  wire clock_1_out, comparator_1_lt, or_3_out;
  wire [1:1] decoder_1_out2;
  wire [12:0] multiplexer_1_out;

  Decoder #(.select(3), .disabled(0), .enable("false")) decoder_1 (
    .out2(decoder_1_out2[1]), .sel(State));  // open: out0, out1, out3, out4, out5, out6, out7
  Multiplexer #(.select(2), .width(13), .disabled(0)) multiplexer_1 (
    .in2(year_in), .in3(13'h7e3), .out(multiplexer_1_out), .sel({decoder_1_out2[1], rst}));  // open: in0, in1, en
  Register #(.width(13)) register_1 (.D(multiplexer_1_out), .Q(Output), .clk(clock_1_out), .clr(in_1));  // open: en
  Clock clock_1 (.out(clock_1_out));
  Comparator #(.width(13)) comparator_1 (.a(multiplexer_1_out), .b({13{1'b0}}), .lt(comparator_1_lt));  // open: gt, eq
  or or_1 (ERR, comparator_1_lt, in_3);
  Comparator #(.width(13)) comparator_2 (
    .a(multiplexer_1_out), .b(13'h7e3), .gt(out_8[2]), .eq(out_8[1]), .lt(out_8[0]));
  or or_2 (Go_Next, or_3_out, Go_Current);
  or or_3 (or_3_out, out_8[0], out_8[2]);

  // Notes on the sheet:
  //   2019 in hex
  //   Check if <0
  //   Check if travel forward/backward
  //   001: Back in time
  //   100: To the future
  //   010: Stay at 2019
endmodule
