// Logisim project Controller.circ as structural Verilog
module Controller (
);

  wire and_1_out, and_2_out, and_3_out, and_4_out, and_5_out, and_6_out, and_7_out, and_8_out, and_9_out,
       clock_1_out, CS0_qn, CS1_qn, CS2_qn, not_1_out, not_2_out, or_1_out, or_2_out, or_3_out;
  wire [1:0] multiplexer_1_out, undriven, undriven_2, undriven_3, undriven_4, undriven_5, undriven_6,
       undriven_7, undriven_8;
  wire [2:0] CS0_q;

  and and_1 (and_1_out, not_1_out, CS0_q[0]);
  not not_1 (not_1_out, multiplexer_1_out[1]);
  and and_2 (and_2_out, not_2_out, CS0_q[1]);
  not not_2 (not_2_out, multiplexer_1_out[1]);
  and and_3 (and_3_out, multiplexer_1_out[1], CS0_qn, CS0_q[1]);
  and and_4 (and_4_out, multiplexer_1_out[1], CS0_q[1], CS0_q[0]);
  and and_5 (and_5_out, multiplexer_1_out[1], CS0_q[0], CS1_qn);
  and and_6 (and_6_out, multiplexer_1_out[1], CS0_q[1], CS0_q[2]);
  and and_7 (and_7_out, multiplexer_1_out[1], CS0_qn, CS0_q[1]);
  and and_8 (and_8_out, CS0_qn, CS0_qn, CS1_qn, CS2_qn);
  or or_1 (or_1_out, multiplexer_1_out[0], CS0_q[2], and_4_out);
  or or_2 (or_2_out, multiplexer_1_out[0], and_2_out, and_5_out, and_7_out, and_9_out);
  and and_9 (and_9_out, multiplexer_1_out[1], CS0_q[1], CS0_q[2]);
  or or_3 (or_3_out, multiplexer_1_out[0], and_1_out, and_3_out, and_6_out, and_8_out);
  Clock clock_1 (.out(clock_1_out));
  D_Flip_Flop CS2 (.clk(clock_1_out), .D(or_1_out), .Q(CS0_q[2]), .Qn(CS2_qn));  // open: preset, en, reset
  D_Flip_Flop CS1 (.clk(clock_1_out), .D(or_2_out), .Q(CS0_q[1]), .Qn(CS1_qn));  // open: preset, en, reset
  D_Flip_Flop CS0 (.clk(clock_1_out), .D(or_3_out), .Q(CS0_q[0]), .Qn(CS0_qn));  // open: preset, en, reset
  Multiplexer #(.select(3), .width(2), .enable("false")) multiplexer_1 (
    .in0(undriven), .in1(undriven_2), .in2(undriven_3), .in3(undriven_4), .in4(undriven_5), .in5(undriven_6),
    .in6(undriven_7), .in7(undriven_8), .out(multiplexer_1_out), .sel(CS0_q));
endmodule
