// Logisim project Destination.circ as structural Verilog: 1 circuit, main circuit main
module main (
  input  Temperature,
  input  Radiation,
  input  Oxygen,
  input  Life,
  input  [8:0] in_5,
  input  [8:0] in_6,
  input  in_7,
  input  [8:0] in_8,
  input  [8:0] in_9,
  input  [8:0] in_10,
  input  [8:0] in_11,
  output [1:0] out_12
);

  wire and_1_out, and_2_out, and_3_out, and_4_out, and_5_out, comparator_1_lt, comparator_2_lt,
       comparator_3_lt, not_1_out;
  wire [8:0] shifter_1_out, shifter_2_out, shifter_3_out;

  Shifter #(.width(9), .shift("lr")) shifter_1 (.in(in_5), .\dist (4'b0010), .out(shifter_1_out));
  Shifter #(.width(9), .shift("lr")) shifter_2 (.in(in_8), .\dist (4'b0010), .out(shifter_2_out));
  Shifter #(.width(9), .shift("lr")) shifter_3 (.in(in_10), .\dist (4'b0010), .out(shifter_3_out));
  not not_1 (not_1_out, Radiation);
  and and_1 (and_1_out, Temperature, not_1_out);
  and and_2 (and_2_out, Oxygen, Life);
  and and_3 (and_3_out, and_1_out, and_2_out);
  Comparator #(.width(9), .mode("unsigned")) comparator_1 (
    .a(shifter_1_out), .b(in_6), .lt(comparator_1_lt));  // open: gt, eq
  Comparator #(.width(9), .mode("unsigned")) comparator_2 (
    .a(shifter_2_out), .b(in_9), .lt(comparator_2_lt));  // open: gt, eq
  Comparator #(.width(9), .mode("unsigned")) comparator_3 (
    .a(shifter_3_out), .b(in_11), .lt(comparator_3_lt));  // open: gt, eq
  and and_4 (and_4_out, comparator_1_lt, comparator_2_lt, comparator_3_lt);
  and and_5 (and_5_out, and_3_out, and_4_out);
  not not_2 (out_12[0], and_5_out);

  assign out_12[1] = in_7;

  // Notes on the sheet:
  //   Altitude check
  //   Latitude
  //   Longitude
  //   Max Value
  //   Habitability (ERR)
endmodule
