// Logisim project FoodWater.circ as structural Verilog: 1 circuit, main circuit main
module main (
  input  [7:0] Food,
  input  [7:0] Water
);

  wire [1:0] comparator_1_eq;
  wire [7:0] adder_1_out;

  Adder adder_1 (.a(Food), .b(Water), .out(adder_1_out));  // open: cin, cout
  Comparator #(.mode("unsigned")) comparator_1 (
    .a(adder_1_out), .b(8'h55), .eq(comparator_1_eq[0]), .lt(comparator_1_eq[1]));  // open: gt
  Multiplexer #(.select(2), .width(2)) multiplexer_1 (.sel(comparator_1_eq));  // open: in0, in1, in2, in3, out, en
endmodule
