// Logisim project Force Circuit.circ as structural Verilog: 6 circuits, main circuit Force Calculation Circuit
module main (
  input  A0,
  input  B0,
  input  D0,
  input  Cin,
  input  A1,
  input  B1,
  input  D1,
  input  A2,
  input  B2,
  input  D2,
  input  A3,
  input  B3,
  input  D3,
  output S0,
  output S0_2,
  output C0,
  output C0_2,
  output S1,
  output S1_2,
  output C1,
  output C1_2,
  output S2,
  output S2_2,
  output C2,
  output C2_2,
  output S3,
  output S3_2,
  output C3,
  output C3_2
);

  wire and_1_out, and_2_out, and_3_out, and_4_out, and_5_out, and_6_out, and_7_out, and_8_out, and_9_out,
       and_10_out, and_11_out, and_12_out, and_13_out, and_14_out, and_15_out, and_16_out, xor_1_out,
       xor_2_out, xor_3_out, xor_4_out, xor_9_out, xor_10_out, xor_11_out, xor_12_out;

  xor xor_1 (xor_1_out, A0, B0);
  xor xor_2 (xor_2_out, A1, B1);
  xor xor_3 (xor_3_out, A2, B2);
  xor xor_4 (xor_4_out, A3, B3);
  and and_1 (and_1_out, Cin, xor_1_out);
  and and_2 (and_2_out, B0, A0);
  and and_3 (and_3_out, C0, xor_2_out);
  and and_4 (and_4_out, B1, A1);
  and and_5 (and_5_out, C1, xor_3_out);
  and and_6 (and_6_out, B2, A2);
  and and_7 (and_7_out, C2, xor_4_out);
  and and_8 (and_8_out, B3, A3);
  xor xor_5 (S0, xor_1_out, Cin);
  or or_1 (C0, and_1_out, and_2_out);
  xor xor_6 (S1, xor_2_out, C0);
  or or_2 (C1, and_3_out, and_4_out);
  xor xor_7 (S2, xor_3_out, C1);
  or or_3 (C2, and_5_out, and_6_out);
  xor xor_8 (S3, xor_4_out, C2);
  or or_4 (C3, and_7_out, and_8_out);
  xor xor_9 (xor_9_out, S0, D0);
  xor xor_10 (xor_10_out, S1, D1);
  xor xor_11 (xor_11_out, S2, D2);
  xor xor_12 (xor_12_out, S3, D3);
  and and_9 (and_9_out, C3, xor_9_out);
  and and_10 (and_10_out, D0, S0);
  and and_11 (and_11_out, C0_2, xor_10_out);
  and and_12 (and_12_out, D1, S1);
  and and_13 (and_13_out, C1_2, xor_11_out);
  and and_14 (and_14_out, D2, S2);
  and and_15 (and_15_out, C2_2, xor_12_out);
  and and_16 (and_16_out, D3, S3);
  xor xor_13 (S0_2, xor_9_out, C3);
  xor xor_14 (S1_2, xor_10_out, C0_2);
  xor xor_15 (S2_2, xor_11_out, C1_2);
  xor xor_16 (S3_2, xor_12_out, C2_2);
  or or_5 (C0_2, and_9_out, and_10_out);
  or or_6 (C1_2, and_11_out, and_12_out);
  or or_7 (C2_2, and_13_out, and_14_out);
  or or_8 (C3_2, and_15_out, and_16_out);

  // Notes on the sheet:
  //   C2-in
  //   C0-in
  //   C1-in
  //   A0 XOR B0
  //   A1 XOR B1
  //   A2 XOR B2
  //   A3 XOR B3
  //   (A0 XOR B0)*(Cin)
  //   (A0)*(B0)
  //   (A1 XOR B1)*(C0-in)
  //   (A1)*(B1)
  //   (A2 XOR B2)*(C1-in)
  //   (A2)*(B2)
  //   (A3 XOR B3)*(C2-in)
  //   (A3)*(B3)
  //   (A2 XOR B2) XOR C1-in
  //   (A0 XOR B0) XOR Cin
  //   [(A0 XOR B0)* (Cin)] + [(A0)*(B0)]
  //   (A1 XOR B1) XOR C0-in
  //   (A3 XOR B3) XOR C2-in
  //   [(A1 XOR B1)* (C0-in)] + [(A1)*(B1)]
  //   [(A2 XOR B2)* (C1-in)] + [(A2)*(B2)]
  //   [(A3 XOR B3)* (C2-in)] + [(A3)*(B3)]
  //   C3-in
  //   S0
  //   S1
  //   S2
  //   S3
  //   C3-in
  //   C1-in
  //   C2-in
  //   A1 XOR B1
  //   C0-in
  //   A2 XOR B2
  //   A3 XOR B3
  //   A0 XOR B0
  //   (A0 XOR B0)*(Cin)
  //   (A0)*(B0)
  //   (A1 XOR B1)*(C0-in)
  //   (A1)*(B1)
  //   (A2 XOR B2)*(C1-in)
  //   (A2)*(B2)
  //   (A3 XOR B3)*(C2-in)
  //   (A3)*(B3)
  //   (A0 XOR B0) XOR Cin
  //   (A1 XOR B1) XOR C0-in
  //   (A2 XOR B2) XOR C1-in
  //   (A3 XOR B3) XOR C2-in
  //   [(A0 XOR B0)* (Cin)] + [(A0)*(B0)]
  //   [(A1 XOR B1)* (C0-in)] + [(A1)*(B1)]
  //   [(A2 XOR B2)* (C1-in)] + [(A2)*(B2)]
  //   [(A3 XOR B3)* (C2-in)] + [(A3)*(B3)]
endmodule

module _4_bit_multiplier (
  input  in_1,
  input  in_2,
  input  in_3,
  input  in_4,
  input  in_5,
  input  in_6,
  input  in_7,
  input  in_8,
  input  in_9,
  input  in_10,
  input  in_11,
  input  in_12,
  input  [3:0] in_13,
  output out_14,
  output out_15,
  output out_16,
  output out_17,
  output out_18,
  output out_19,
  output out_20,
  output out_21,
  output out_22,
  output [3:0] out_23,
  output [3:0] out_24
);

  wire adder_1_cout, adder_2_cout, adder_3_cout, adder_4_cout, adder_5_cout, adder_6_cout, adder_7_cout;

  Adder #(.width(1)) adder_1 (.a(in_4), .b(in_8), .out(out_17), .cin(1'b0), .cout(adder_1_cout));
  Adder #(.width(1)) adder_2 (.a(out_17), .b(in_12), .out(out_22), .cin(adder_7_cout), .cout(adder_2_cout));
  Adder #(.width(1)) adder_3 (.a(in_1), .b(in_5), .out(out_14), .cin(adder_1_cout), .cout(adder_3_cout));
  Adder #(.width(1)) adder_4 (.a(out_14), .b(in_9), .out(out_18), .cin(adder_2_cout), .cout(adder_4_cout));
  Multiplier #(.width(4)) multiplier_1 (
    .a(in_13), .b({out_20, out_19, out_18, out_22}), .out(out_23), .cout(out_24));  // open: cin
  Adder #(.width(1)) adder_5 (.a(in_2), .b(in_6), .out(out_15), .cin(adder_3_cout), .cout(adder_5_cout));
  Adder #(.width(1)) adder_6 (.a(out_15), .b(in_10), .out(out_19), .cin(adder_4_cout), .cout(adder_6_cout));
  Adder #(.width(1)) adder_7 (.a(in_3), .b(in_7), .out(out_16), .cin(adder_5_cout), .cout(adder_7_cout));
  Adder #(.width(1)) adder_8 (.a(out_16), .b(in_11), .out(out_20), .cin(adder_6_cout), .cout(out_21));
endmodule

module _4_bit_Full_Adder (
  input  A0,
  input  B0,
  input  Cin,
  input  A1,
  input  B1,
  input  A2,
  input  B2,
  input  A3,
  input  B3,
  output S0,
  output C0,
  output S1,
  output C1,
  output S2,
  output C2,
  output S3,
  output C3
);

  wire and_1_out, and_2_out, and_3_out, and_4_out, and_5_out, and_6_out, and_7_out, and_8_out, xor_1_out,
       xor_2_out, xor_3_out, xor_4_out;

  xor xor_1 (xor_1_out, A0, B0);
  xor xor_2 (xor_2_out, A1, B1);
  xor xor_3 (xor_3_out, A2, B2);
  xor xor_4 (xor_4_out, A3, B3);
  and and_1 (and_1_out, Cin, xor_1_out);
  and and_2 (and_2_out, B0, A0);
  and and_3 (and_3_out, C0, xor_2_out);
  and and_4 (and_4_out, B1, A1);
  and and_5 (and_5_out, C1, xor_3_out);
  and and_6 (and_6_out, B2, A2);
  and and_7 (and_7_out, C2, xor_4_out);
  and and_8 (and_8_out, B3, A3);
  xor xor_5 (S0, xor_1_out, Cin);
  or or_1 (C0, and_1_out, and_2_out);
  xor xor_6 (S1, xor_2_out, C0);
  or or_2 (C1, and_3_out, and_4_out);
  xor xor_7 (S2, xor_3_out, C1);
  or or_3 (C2, and_5_out, and_6_out);
  xor xor_8 (S3, xor_4_out, C2);
  or or_4 (C3, and_7_out, and_8_out);

  // Notes on the sheet:
  //   C2-in
  //   C0-in
  //   C1-in
  //   A0 XOR B0
  //   A1 XOR B1
  //   A2 XOR B2
  //   A3 XOR B3
  //   (A0 XOR B0)*(Cin)
  //   (A0)*(B0)
  //   (A1 XOR B1)*(C0-in)
  //   (A1)*(B1)
  //   (A2 XOR B2)*(C1-in)
  //   (A2)*(B2)
  //   (A3 XOR B3)*(C2-in)
  //   (A3)*(B3)
  //   (A2 XOR B2) XOR C1-in
  //   (A0 XOR B0) XOR Cin
  //   [(A0 XOR B0)* (Cin)] + [(A0)*(B0)]
  //   (A1 XOR B1) XOR C0-in
  //   (A3 XOR B3) XOR C2-in
  //   [(A1 XOR B1)* (C0-in)] + [(A1)*(B1)]
  //   [(A2 XOR B2)* (C1-in)] + [(A2)*(B2)]
  //   [(A3 XOR B3)* (C2-in)] + [(A3)*(B3)]
endmodule

module _4_bit_Multiplication_Logic_Diagram (
  input  [3:0] Passengers,
  input  [3:0] Crew,
  input  [3:0] Resources,
  input  [3:0] Acceleration,
  output [3:0] out_5,
  output [3:0] out_6,
  output [3:0] out_7,
  output [3:0] out_8,
  output [3:0] out_9,
  output [7:0] out_10
);

  wire adder_1_cout;
  wire [3:0] and_15_out;
  wire [3:1] adder_3_out, adder_4_out;
  wire [3:3] adder_3_cout, adder_4_cout;

  Adder #(.width(4)) adder_1 (.a(Passengers), .b(Crew), .out(out_5), .cin(1'b0), .cout(adder_1_cout));
  Adder #(.width(4)) adder_2 (.a(out_5), .b(Resources), .out(out_6), .cin(adder_1_cout), .cout(and_15_out[3]));
  and and_1 (out_7[3], Acceleration[1], out_6[3]);
  and and_2 (out_8[3], Acceleration[2], out_6[3]);
  and and_3 (out_9[3], Acceleration[3], out_6[3]);
  and and_4 (out_7[2], Acceleration[1], out_6[2]);
  and and_5 (out_8[2], Acceleration[2], out_6[2]);
  and and_6 (out_8[1], Acceleration[2], out_6[1]);
  and and_7 (out_9[2], Acceleration[3], out_6[2]);
  and and_8 (out_9[1], Acceleration[3], out_6[1]);
  and and_9 (out_7[0], Acceleration[1], out_6[0]);
  and and_10 (out_7[1], Acceleration[1], out_6[1]);
  and and_11 (out_8[0], Acceleration[2], out_6[0]);
  and and_12 (out_9[0], Acceleration[3], out_6[0]);
  Adder #(.width(4)) adder_3 (
    .a(out_7), .b(and_15_out), .out({adder_3_out, out_10[1]}), .cin(1'b0), .cout(adder_3_cout[3]));
  Adder #(.width(4)) adder_4 (
    .a(out_8), .b({adder_3_cout[3], adder_3_out}), .out({adder_4_out, out_10[2]}), .cin(1'b0),
    .cout(adder_4_cout[3]));
  Adder #(.width(4)) adder_5 (
    .a(out_9), .b({adder_4_cout[3], adder_4_out}), .out(out_10[6:3]), .cin(1'b0), .cout(out_10[7]));
  and and_13 (and_15_out[2], Acceleration[0], out_6[3]);
  and and_14 (and_15_out[1], Acceleration[0], out_6[2]);
  and and_15 (and_15_out[0], Acceleration[0], out_6[1]);
  and and_16 (out_10[0], Acceleration[0], out_6[0]);

  // Notes on the sheet:
  //   Passengers + Crew
  //   (Pasengers + Crew) + Resources
  //   4-Bit Multiplication Logic Diagram
  //   Mass
  //   = Mass
  //   2
  //   3
  //   1
  //   Mass * Acceleration = Force
  //   0
endmodule

module Force_Calculation_Circuit (
  input  [3:0] Max_5,
  input  [3:0] in_2,
  input  [7:0] Max_15,
  input  [7:0] in_4,
  input  [3:0] in_5,
  input  [7:0] in_6,
  input  [3:0] in_7,
  input  [7:0] in_8,
  output [3:0] Passeners___Crew,
  output [7:0] Passeners___Crew_2,
  output [3:0] out_11,
  output [7:0] out_12,
  output [3:0] F3____F0,
  output [7:0] out_14,
  output [3:0] F7____F4,
  output [7:0] out_16
);

  wire adder_1_cout, adder_3_cout;

  Adder adder_1 (.a(Max_15), .b(in_4), .out(Passeners___Crew_2), .cin(1'b0), .cout(adder_1_cout));
  Adder adder_2 (.a(Passeners___Crew_2), .b(in_6), .out(out_12), .cin(adder_1_cout));  // open: cout
  Multiplier multiplier_1 (.a(out_12), .b(in_8), .out(out_14), .cout(out_16));  // open: cin
  Adder #(.width(4)) adder_3 (.a(Max_5), .b(in_2), .out(Passeners___Crew), .cin(1'b0), .cout(adder_3_cout));
  Adder #(.width(4)) adder_4 (.a(Passeners___Crew), .b(in_5), .out(out_11), .cin(adder_3_cout));  // open: cout
  Multiplier #(.width(4)) multiplier_2 (.a(out_11), .b(in_7), .out(F3____F0), .cout(F7____F4));  // open: cin

  // Notes on the sheet:
  //   8 Bit Multiplier
  //   Passengers
  //   Crew
  //   (Max 4)
  //   Resrouces
  //   (Max 16)
  //   Acceleration
  //   3 * 10^8 m/s
  //   Force = Mass *Acceleration Circuit Diagram
  //   Passeners + Crew
  //   Mass
  //   Mass * Acceleration = Force = F7,...,F0
  //   (Passengers + Crew) + Resources = Mass
  //   Passengers
  //   Crew
  //   (Max 3)
  //   Resrouces
  //   (Max 7)
  //   Acceleration
  //   3 * 10^8 m/s
  //   4 Bit Multiplier
  //   Force = Mass *Acceleration Circuit Diagram
  //   Passeners + Crew
  //   Mass
  //   (Passengers + Crew) + Resources = Mass
  //   Mass * Acceleration = Force = F7,...,F0
endmodule

module Final_4_bit_Multiplication (
  input  [3:0] Max_5,
  input  [3:0] in_2,
  input  [3:0] in_3,
  input  [3:0] in_4,
  output [3:0] Passeners___Crew,
  output [3:0] out_6,
  output [3:0] F3____F0,
  output [3:0] F7____F4
);

  wire adder_1_cout;

  Adder #(.width(4)) adder_1 (.a(Max_5), .b(in_2), .out(Passeners___Crew), .cin(1'b0), .cout(adder_1_cout));
  Adder #(.width(4)) adder_2 (.a(Passeners___Crew), .b(in_3), .out(out_6), .cin(adder_1_cout));  // open: cout
  Multiplier #(.width(4)) multiplier_1 (.a(out_6), .b(in_4), .out(F3____F0), .cout(F7____F4));  // open: cin

  // Notes on the sheet:
  //   Passengers
  //   Crew
  //   (Max 3)
  //   Resrouces
  //   (Max 7)
  //   Acceleration
  //   3 * 10^8 m/s
  //   Force = Mass *Acceleration Circuit Diagram (4-bit Multiplier)
  //   Passeners + Crew
  //   Mass
  //   Mass * Acceleration = Force = F7,...,F0
  //   (Passengers + Crew) + Resources = Mass
endmodule
