// Logisim project Load Ship.circ as structural Verilog: 4 circuits, main circuit main
module main (
  input  User_Input__A,
  input  in_2,
  input  in_3,
  input  in_4,
  input  in_5,
  input  in_6,
  input  in_7,
  input  in_8,
  input  in_9,
  input  User_Input__A_2,
  input  in_11,
  input  in_12,
  input  in_13,
  input  in_14,
  input  in_15,
  input  in_16,
  input  User_Input__A_3,
  input  in_18,
  input  in_19,
  input  in_20,
  input  in_21,
  input  in_22,
  input  in_23,
  input  in_24,
  output out_25
);

  wire Comparator_2_out_9, Comparator_out_9, Equals_out_9;

  Comparator Comparator (
    .A3(User_Input__A), .B3(in_2), .A2(in_3), .in_4(in_4), .A1(in_5), .in_6(in_6), .in_7(in_7), .B0(in_8),
    .out_9(Comparator_out_9));
  Comparator Comparator_2 (
    .A3(in_9), .B3(User_Input__A_2), .A2(in_11), .in_4(in_12), .A1(in_13), .in_6(in_14), .in_7(in_15),
    .B0(in_16), .out_9(Comparator_2_out_9));
  Equals Equals (
    .A3(User_Input__A_3), .out_9(Equals_out_9), .B3(in_18), .A2(in_19), .B2(in_20), .A1(in_21), .B1(in_22),
    .A0(in_23), .B0(in_24));
  and and_1 (out_25, Comparator_out_9, Comparator_2_out_9, Equals_out_9);

  // Notes on the sheet:
  //   Max Passengers (B) - (1111) 15
  //   Crew (B) - 0100 (4)
  //   Cargo Space (B) - 1111 (16 pounds)
endmodule

module Comparator (
  input  A3,
  input  B3,
  input  A2,
  input  in_4,
  input  A1,
  input  in_6,
  input  in_7,
  input  B0,
  output out_9
);

  wire and_1_out, and_2_out, and_3_out, and_4_out, and_5_out, and_6_out, and_7_out, and_8_out, and_9_out,
       and_10_out, and_11_out, and_12_out, nor_1_out, nor_2_out, nor_3_out, nor_4_out, not_1_out, not_2_out,
       not_3_out, not_4_out, not_5_out, not_6_out, not_7_out, not_8_out, or_1_out;

  not not_1 (not_1_out, A3);
  not not_2 (not_2_out, B3);
  not not_3 (not_3_out, A2);
  not not_4 (not_4_out, in_4);
  not not_5 (not_5_out, A1);
  not not_6 (not_6_out, in_6);
  not not_7 (not_7_out, in_7);
  not not_8 (not_8_out, B0);
  and and_1 (and_1_out, not_1_out, B3);
  and and_2 (and_2_out, A3, not_2_out, not_2_out);
  and and_3 (and_3_out, not_3_out, in_4);
  and and_4 (and_4_out, A2, not_4_out);
  and and_5 (and_5_out, not_5_out, in_6);
  and and_6 (and_6_out, A1, not_6_out);
  and and_7 (and_7_out, not_7_out, B0);
  and and_8 (and_8_out, in_7, not_8_out);
  nor nor_1 (nor_1_out, and_1_out, and_2_out);
  nor nor_2 (nor_2_out, and_3_out, and_4_out);
  nor nor_3 (nor_3_out, and_5_out, and_6_out);
  nor nor_4 (nor_4_out, and_7_out, and_8_out);
  and and_9 (and_9_out, nor_1_out, nor_2_out, nor_3_out, nor_4_out);
  and and_10 (and_10_out, nor_1_out, and_3_out);
  and and_11 (and_11_out, nor_1_out, nor_2_out, and_5_out);
  and and_12 (and_12_out, nor_1_out, nor_2_out, nor_3_out, and_7_out);
  or or_1 (or_1_out, and_1_out, and_10_out, and_11_out, and_12_out);
  or or_2 (out_9, or_1_out, and_9_out);
endmodule

module Equals (
  input  A3,
  input  B3,
  input  A2,
  input  B2,
  input  A1,
  input  B1,
  input  A0,
  input  B0,
  output out_9
);

  wire xnor_1_out, xnor_2_out, xnor_3_out, xnor_4_out;

  xnor xnor_1 (xnor_1_out, A3, B3);
  xnor xnor_2 (xnor_2_out, A2, B2);
  xnor xnor_3 (xnor_3_out, A1, B1);
  xnor xnor_4 (xnor_4_out, A0, B0);
  and and_1 (out_9, xnor_1_out, xnor_2_out, xnor_3_out, xnor_4_out);
endmodule

module TestCircuit (
  input  in_1,
  input  in_2,
  input  [2:0] in_3,
  input  [2:0] in_4,
  input  [2:0] in_5,
  input  [2:0] in_6,
  input  [2:0] in_7,
  input  [2:0] in_8,
  input  [2:0] in_9,
  input  [2:0] in_10,
  input  [2:0] in_11,
  output out_12,
  output out_13,
  output out_14,
  output out_15,
  output [2:0] out_16
);

  wire and_1_out, and_2_out, and_3_out, clock_1_out, d_ff_1_qn, d_ff_2_qn, not_1_out, or_1_out, or_2_out;

  and and_1 (and_1_out, out_12, in_1);
  and and_2 (and_2_out, in_1, out_13);
  and and_3 (and_3_out, in_1, d_ff_1_qn);
  or or_1 (or_1_out, out_13, out_12);
  not not_1 (not_1_out, in_1);
  or or_2 (or_2_out, and_1_out, and_1_out, and_2_out);
  Clock clock_1 (.out(clock_1_out));
  D_Flip_Flop d_ff_1 (.clk(clock_1_out), .D(or_2_out), .Q(out_12), .Qn(d_ff_1_qn));  // open: preset, en, reset
  D_Flip_Flop d_ff_2 (.clk(clock_1_out), .D(and_3_out), .Q(out_13), .Qn(d_ff_2_qn));  // open: preset, en, reset
  and and_4 (out_15, or_1_out, not_1_out);
  Multiplexer #(.select(3), .width(3)) multiplexer_1 (
    .in0(in_3), .in1(in_4), .in2(in_5), .in3(in_6), .in4(in_7), .in5(in_8), .in6(in_9), .in7(in_10),
    .out(out_16), .sel(in_11));  // open: en
  D_Flip_Flop d_ff_3 (.clk(clock_1_out), .D(in_2), .Q(out_14));  // open: Qn, preset, en, reset
endmodule
